// Logisim project OneBit.circ as structural Verilog: 7 circuits, main circuit main
module main (
  input  W,
  input  R,
  input  in_3,
  input  W_2,
  input  R_2,
  input  W_3,
  input  R_3,
  input  W_4,
  input  R_4,
  input  W_5,
  input  R_5
);

  wire Bus_memory, Bus_write_data, Cell_0_memory, Cell_0_write_data, Cell_1_memory, Cell_1_write_data,
       or_2_out, undriven, undriven_2, X_memory, X_write_data, Y_memory, Y_write_data;

  // Probe on Cell_0_memory
  // Probe on Cell_1_memory
  Register4 Cell_0 (.Read(R), .Read_Data(undriven), .Write(W), .Write_Data(Cell_0_write_data), .Memory(Cell_0_memory));
  Register4 Cell_1 (
    .Read(R_4), .Read_Data(undriven_2), .Write(W_4), .Write_Data(Cell_1_write_data), .Memory(Cell_1_memory));
  // OR_Gate or_1 is placed but not wired
  or or_2 (or_2_out, in_3, Bus_write_data, Y_write_data, X_write_data);
  // OR_Gate or_3 is placed but not wired
  // Probe on X_memory
  // Probe on Y_memory
  // Probe on Bus_memory
  Register4 X (.Read(R_2), .Read_Data(or_2_out), .Write(W_2), .Write_Data(X_write_data), .Memory(X_memory));
  Register4 Y (.Read(R_3), .Read_Data(or_2_out), .Write(W_3), .Write_Data(Y_write_data), .Memory(Y_memory));
  Register4 Bus (.Read(R_5), .Read_Data(or_2_out), .Write(W_5), .Write_Data(Bus_write_data), .Memory(Bus_memory));
endmodule

module Register (
  input  In_Bus,
  input  Clock,
  input  Read,
  input  Write
);

  wire and_1_out, and_2_out, and_3_out, nand_1_out, nand_2_out, nand_3_out, nand_4_out, not_1_out, or_1_out;

  or or_1 (or_1_out, In_Bus, and_1_out);
  and and_1 (and_1_out, nand_4_out, Write);
  and and_2 (and_2_out, Clock, Read);
  and and_3 (and_3_out, Read, or_1_out);
  not not_1 (not_1_out, and_3_out);
  nand nand_1 (nand_1_out, not_1_out, and_2_out);
  nand nand_2 (nand_2_out, and_2_out, and_3_out);
  nand nand_3 (nand_3_out, nand_1_out, nand_4_out);
  nand nand_4 (nand_4_out, nand_3_out, nand_2_out);

  // Notes on the sheet:
  //   Data
endmodule

module Register2 (
  input  In_Bus,
  input  Read,
  input  Write
);

  wire and_1_out, nand_1_out, nand_2_out, nand_3_out, nand_4_out, nand_5_out, not_1_out, or_1_out;

  or or_1 (or_1_out, In_Bus, and_1_out);
  nand nand_1 (nand_1_out, Read, or_1_out);
  and and_1 (and_1_out, nand_5_out, Write);
  not not_1 (not_1_out, nand_1_out);
  nand nand_2 (nand_2_out, nand_1_out, Read);
  nand nand_3 (nand_3_out, Read, not_1_out);
  nand nand_4 (nand_4_out, nand_2_out, nand_5_out);
  nand nand_5 (nand_5_out, nand_4_out, nand_3_out);

  // Notes on the sheet:
  //   Data
endmodule

module Register3 (
  input  In_Bus,
  input  Read,
  input  Write
);

  wire nand_1_out, nand_2_out, nand_3_out, nand_4_out, nand_5_out, nand_6_out, not_1_out, not_2_out, or_1_out;

  or or_1 (or_1_out, In_Bus, not_2_out);
  nand nand_1 (nand_1_out, Read, or_1_out);
  nand nand_2 (nand_2_out, nand_6_out, Write);
  not not_1 (not_1_out, nand_1_out);
  not not_2 (not_2_out, nand_2_out);
  nand nand_3 (nand_3_out, nand_1_out, Read);
  nand nand_4 (nand_4_out, Read, not_1_out);
  nand nand_5 (nand_5_out, nand_3_out, nand_6_out);
  nand nand_6 (nand_6_out, nand_5_out, nand_4_out);

  // Notes on the sheet:
  //   Read Data
  //   Write Data
endmodule

module Register4 (
  input  Read,
  input  Read_Data,
  input  Write,
  output Write_Data,
  output Memory
);

  wire nand_1_out, nand_2_out, nand_3_out, nand_4_out, nand_5_out, not_2_out;

  nand nand_1 (nand_1_out, Read, Read_Data);
  nand nand_2 (nand_2_out, Memory, Write);
  not not_1 (Write_Data, nand_2_out);
  not not_2 (not_2_out, nand_1_out);
  nand nand_3 (nand_3_out, nand_1_out, Read);
  nand nand_4 (nand_4_out, Read, not_2_out);
  nand nand_5 (nand_5_out, nand_3_out, Memory);
  nand nand_6 (Memory, nand_5_out, nand_4_out);
endmodule

module T_Trigger (
  input  Read
);

  wire nand_1_out, nand_2_out, nand_3_out, nand_4_out, nand_5_out, nand_6_out, nand_7_out, nand_8_out,
       not_1_out;

  not not_1 (not_1_out, Read);
  nand nand_1 (nand_1_out, nand_8_out, Read);
  nand nand_2 (nand_2_out, Read, nand_7_out);
  nand nand_3 (nand_3_out, nand_1_out, nand_4_out);
  nand nand_4 (nand_4_out, nand_3_out, nand_2_out);
  nand nand_5 (nand_5_out, nand_3_out, not_1_out);
  nand nand_6 (nand_6_out, not_1_out, nand_4_out);
  nand nand_7 (nand_7_out, nand_5_out, nand_8_out);
  nand nand_8 (nand_8_out, nand_7_out, nand_6_out);
endmodule

module T_Trigger2 (
  input  in_1
);

  wire nand_1_out, nand_2_out, nand_3_out, nand_4_out, nand_5_out, nand_6_out;

  nand nand_1 (nand_1_out, in_1, nand_2_out);
  nand nand_2 (nand_2_out, nand_1_out, nand_4_out);
  nand nand_3 (nand_3_out, nand_1_out, in_1, nand_4_out);
  nand nand_4 (nand_4_out, nand_3_out, nand_6_out);
  nand nand_5 (nand_5_out, nand_1_out, nand_6_out);
  nand nand_6 (nand_6_out, nand_5_out, nand_3_out);
endmodule
